// Logisim project Github_Now.circ as structural Verilog: 9 circuits, main circuit main
module main (
  input  [7:0] Y,
  input  [7:0] X,
  input  LD,
  input  R,
  input  CLK,
  output Sign_bit,
  output [15:0] P,
  output Product,
  output LED0
);

  wire and_1_out, and_2_out, and_3_out, and_4_out, and_5_out, and_6_out, and_7_out, and_8_out, BTNL_out,
       BTNR_out, csadd_1_sum, csadd_2_sum, csadd_3_sum, csadd_4_sum, csadd_5_sum, csadd_6_sum,
       current_y_bit_1_current_y, multiplexer_1_out, not_1_out, tcmp_1_s;
  wire [3:0] binary_to_bcd_1_d0, binary_to_bcd_1_d1, binary_to_bcd_1_d2, binary_to_bcd_1_d3,
       binary_to_bcd_1_d4;

  TCMP tcmp_1 (.A(and_1_out), .CLK(CLK), .R(R), .S(tcmp_1_s));
  and and_1 (and_1_out, X[7], current_y_bit_1_current_y);
  and and_2 (and_2_out, X[6], current_y_bit_1_current_y);
  and and_3 (and_3_out, X[5], current_y_bit_1_current_y);
  CSADD csadd_1 (.X(and_2_out), .Y(tcmp_1_s), .R(R), .CLK(CLK), .SUM(csadd_1_sum));
  and and_4 (and_4_out, X[4], current_y_bit_1_current_y);
  and and_5 (and_5_out, X[3], current_y_bit_1_current_y);
  CSADD csadd_2 (.X(and_3_out), .Y(csadd_1_sum), .R(R), .CLK(CLK), .SUM(csadd_2_sum));
  CSADD csadd_3 (.X(and_4_out), .Y(csadd_2_sum), .R(R), .CLK(CLK), .SUM(csadd_3_sum));
  and and_6 (and_6_out, X[2], current_y_bit_1_current_y);
  and and_7 (and_7_out, X[1], current_y_bit_1_current_y);
  CSADD csadd_4 (.X(and_5_out), .Y(csadd_3_sum), .R(R), .CLK(CLK), .SUM(csadd_4_sum));
  and and_8 (and_8_out, X[0], current_y_bit_1_current_y);
  CSADD csadd_5 (.X(and_6_out), .Y(csadd_4_sum), .R(R), .CLK(CLK), .SUM(csadd_5_sum));
  CSADD csadd_6 (.X(and_7_out), .Y(csadd_5_sum), .R(R), .CLK(CLK), .SUM(csadd_6_sum));
  CSADD csadd_7 (.X(and_8_out), .Y(csadd_6_sum), .R(R), .CLK(CLK), .SUM(Product));
  Current_Y_bit current_y_bit_1 (.Y(Y), .R(R), .CLK(CLK), .Current_Y(current_y_bit_1_current_y));
  Product_Load product_load_1 (.Current_P(Product), .R(R), .CLK(CLK), .Product(P), .Done_Next(LED0));
  not not_1 (not_1_out, P[15]);
  Binary_to_BCD binary_to_bcd_1 (
    .Binary_IN(P), .D4(binary_to_bcd_1_d4), .D3(binary_to_bcd_1_d3), .D2(binary_to_bcd_1_d2),
    .D1(binary_to_bcd_1_d1), .D0(binary_to_bcd_1_d0));
  _7_Segment_Display Sign_digit (
    .f(multiplexer_1_out), .a(not_1_out), .b(not_1_out), .e(multiplexer_1_out), .d(not_1_out), .c(not_1_out));  // open: g, dp
  Multiplexer multiplexer_1 (.in0(not_1_out), .in1(P[15]), .out(multiplexer_1_out), .sel(P[15]));
  _7_Segment_Display u_7_segment_display_1 ();  // open: g, f, a, b, e, d, c, dp
  // BCD_to_7_Segment_decoder bcd_to_7_segment_decoder_1: pin names not known; wires that end beside it: P[15], binary_to_bcd_1_d4
  Button BTNR (.out(BTNR_out));
  Button BTNL (.out(BTNL_out));
  _7_Segment_Display u_7_segment_display_2 ();  // open: g, f, a, b, e, d, c, dp
  // BCD_to_7_Segment_decoder bcd_to_7_segment_decoder_2: pin names not known; wires that end beside it: binary_to_bcd_1_d3
  _7_Segment_Display u_7_segment_display_3 ();  // open: g, f, a, b, e, d, c, dp
  // BCD_to_7_Segment_decoder bcd_to_7_segment_decoder_3: pin names not known; wires that end beside it: binary_to_bcd_1_d2
  Multiplexer multiplexer_2 (.in0(BTNR_out), .in1(BTNL_out));  // open: out, sel
  _7_Segment_Display u_7_segment_display_4 ();  // open: g, f, a, b, e, d, c, dp
  // BCD_to_7_Segment_decoder bcd_to_7_segment_decoder_4: pin names not known; wires that end beside it: binary_to_bcd_1_d1
  _7_Segment_Display u_7_segment_display_5 ();  // open: g, f, a, b, e, d, c, dp
  // BCD_to_7_Segment_decoder bcd_to_7_segment_decoder_5: pin names not known; wires that end beside it: binary_to_bcd_1_d0

  assign Sign_bit = P[15];
endmodule

module HA (
  input  D0,
  input  D1,
  output Sum,
  output CO
);

  and and_1 (CO, D0, D1);
  xor xor_1 (Sum, D0, D1);
endmodule

module CSADD (
  input  X,
  input  Y,
  input  R,
  input  CLK,
  output SUM
);

  wire and_1_out, d_ff_2_q, ha_1_co, ha_1_sum, xor_1_out, xor_2_out;

  and and_1 (and_1_out, ha_1_sum, X);
  xor xor_1 (xor_1_out, X, ha_1_sum);
  D_Flip_Flop d_ff_1 (.D(xor_1_out), .clk(CLK), .Q(SUM), .reset(R));  // open: Qn, preset
  HA ha_1 (.D0(Y), .D1(d_ff_2_q), .Sum(ha_1_sum), .CO(ha_1_co));
  D_Flip_Flop d_ff_2 (.D(xor_2_out), .clk(CLK), .Q(d_ff_2_q), .reset(R));  // open: Qn, preset
  xor xor_2 (xor_2_out, and_1_out, ha_1_co);
endmodule

module TCMP (
  input  A,
  input  CLK,
  input  R,
  output S
);

  wire d_ff_1_q, or_1_out, xor_1_out;

  xor xor_1 (xor_1_out, A, d_ff_1_q);
  D_Flip_Flop d_ff_1 (.D(or_1_out), .clk(CLK), .Q(d_ff_1_q), .reset(R));  // open: Qn, preset
  or or_1 (or_1_out, A, d_ff_1_q);
  D_Flip_Flop d_ff_2 (.D(xor_1_out), .clk(CLK), .Q(S), .reset(R));  // open: Qn, preset
endmodule

module Current_Y_bit (
  input  [7:0] Y,
  input  R,
  input  CLK,
  output Current_Y
);

  wire comparator_1_eq;
  wire [2:0] counter_1_q;

  Multiplexer #(.select(3)) multiplexer_1 (
    .in0(Y[0]), .in1(Y[1]), .in2(Y[2]), .in3(Y[3]), .in4(Y[4]), .in5(Y[5]), .in6(Y[6]), .in7(Y[7]),
    .out(Current_Y), .sel(counter_1_q));
  Counter #(.max('h7), .width(3)) counter_1 (
    .clr(R), .load(comparator_1_eq), .up(1'b1), .count(1'b1), .clk(CLK), .Q(counter_1_q));  // open: D, carry
  Comparator #(.width(3)) comparator_1 (.a(3'b111), .b(counter_1_q), .eq(comparator_1_eq));  // open: gt, lt
endmodule

module Product_Load (
  input  Current_P,
  input  R,
  input  CLK,
  output [15:0] Product,
  output Done_Next
);

  wire not_1_out;
  wire [4:0] counter_1_q;

  not not_1 (not_1_out, Done_Next);
  // Shift_Register #(.length(16)) shift_register_1: pin names not known; wires that end beside it: R, 1'b0, not_1_out, CLK, Current_P, 1'b0, 1'b0, 1'b0, 1'b0, 1'b0, 1'b0, 1'b0, 1'b0, 1'b0, 1'b0, 1'b0, 1'b0, Product[15], Product[14], Product[13], Product[12], Product[11], Product[10], Product[9], Product[8], Product[7], Product[6], Product[5], Product[4]
  Counter #(.max('h11), .width(5)) counter_1 (
    .clr(R), .load(Done_Next), .up(1'b1), .count(1'b1), .clk(CLK), .Q(counter_1_q));  // open: D, carry
  Comparator #(.width(5)) comparator_1 (.a(5'b10001), .b(counter_1_q), .eq(Done_Next));  // open: gt, lt
endmodule

module Binary_to_BCD (
  input  [15:0] Binary_IN,
  output [3:0] D4,
  output [3:0] D3,
  output [3:0] D2,
  output [3:0] D1,
  output [3:0] D0
);

  wire conditional_increment_by3_2_out0, conditional_increment_by3_2_out1, conditional_increment_by3_2_out2,
       conditional_increment_by3_2_out3, conditional_increment_by3_3_out0, conditional_increment_by3_3_out1,
       conditional_increment_by3_3_out2, conditional_increment_by3_3_out3, conditional_increment_by3_4_out0,
       conditional_increment_by3_4_out1, conditional_increment_by3_4_out2, conditional_increment_by3_4_out3,
       conditional_increment_by3_7_out0, conditional_increment_by3_7_out1, conditional_increment_by3_7_out2,
       conditional_increment_by3_7_out3, conditional_increment_by3_8_out0, conditional_increment_by3_8_out1,
       conditional_increment_by3_8_out2, conditional_increment_by3_8_out3, conditional_increment_by3_9_out0,
       conditional_increment_by3_9_out1, conditional_increment_by3_9_out2, conditional_increment_by3_9_out3,
       conditional_increment_by3_10_out0, conditional_increment_by3_10_out1,
       conditional_increment_by3_10_out2, conditional_increment_by3_10_out3,
       conditional_increment_by3_11_out0, conditional_increment_by3_11_out1,
       conditional_increment_by3_11_out2, conditional_increment_by3_11_out3,
       conditional_increment_by3_12_out0, conditional_increment_by3_12_out1,
       conditional_increment_by3_12_out2, conditional_increment_by3_12_out3,
       conditional_increment_by3_13_out0, conditional_increment_by3_13_out1,
       conditional_increment_by3_13_out2, conditional_increment_by3_13_out3,
       conditional_increment_by3_14_out0, conditional_increment_by3_14_out1,
       conditional_increment_by3_14_out2, conditional_increment_by3_14_out3,
       conditional_increment_by3_15_out0, conditional_increment_by3_15_out1,
       conditional_increment_by3_15_out2, conditional_increment_by3_15_out3,
       conditional_increment_by3_16_out0, conditional_increment_by3_16_out1,
       conditional_increment_by3_16_out2, conditional_increment_by3_16_out3,
       conditional_increment_by3_17_out0, conditional_increment_by3_17_out1,
       conditional_increment_by3_17_out2, conditional_increment_by3_17_out3,
       conditional_increment_by3_18_out0, conditional_increment_by3_18_out1,
       conditional_increment_by3_18_out2, conditional_increment_by3_18_out3,
       conditional_increment_by3_19_out0, conditional_increment_by3_19_out1,
       conditional_increment_by3_19_out2, conditional_increment_by3_19_out3,
       conditional_increment_by3_20_out0, conditional_increment_by3_20_out1,
       conditional_increment_by3_20_out2, conditional_increment_by3_20_out3,
       conditional_increment_by3_21_out0, conditional_increment_by3_21_out1,
       conditional_increment_by3_21_out2, conditional_increment_by3_21_out3,
       conditional_increment_by3_22_out0, conditional_increment_by3_22_out1,
       conditional_increment_by3_22_out2, conditional_increment_by3_22_out3,
       conditional_increment_by3_23_out0, conditional_increment_by3_23_out1,
       conditional_increment_by3_23_out2, conditional_increment_by3_23_out3,
       conditional_increment_by3_24_out0, conditional_increment_by3_24_out1,
       conditional_increment_by3_24_out2, conditional_increment_by3_24_out3,
       conditional_increment_by3_25_out0, conditional_increment_by3_25_out1,
       conditional_increment_by3_25_out2, conditional_increment_by3_25_out3,
       conditional_increment_by3_26_out0, conditional_increment_by3_26_out1,
       conditional_increment_by3_26_out2, conditional_increment_by3_26_out3,
       conditional_increment_by3_27_out0, conditional_increment_by3_27_out1,
       conditional_increment_by3_27_out2, conditional_increment_by3_27_out3,
       conditional_increment_by3_30_out0, conditional_increment_by3_30_out1,
       conditional_increment_by3_30_out2, conditional_increment_by3_30_out3,
       conditional_increment_by3_31_out0, conditional_increment_by3_31_out1,
       conditional_increment_by3_31_out2, conditional_increment_by3_31_out3,
       conditional_increment_by3_32_out0, conditional_increment_by3_32_out1,
       conditional_increment_by3_32_out2, conditional_increment_by3_32_out3,
       conditional_increment_by3_33_out0, conditional_increment_by3_33_out1,
       conditional_increment_by3_33_out2, conditional_increment_by3_33_out3,
       conditional_increment_by3_34_out0, conditional_increment_by3_34_out1,
       conditional_increment_by3_34_out2, conditional_increment_by3_34_out3,
       conditional_increment_by3_35_out0, conditional_increment_by3_35_out1,
       conditional_increment_by3_35_out2, conditional_increment_by3_35_out3;

  Conditional_Increment_by3 conditional_increment_by3_1 (
    .IN3(1'b0), .IN2(conditional_increment_by3_3_out3), .IN1(conditional_increment_by3_2_out3),
    .IN0(conditional_increment_by3_7_out3), .OUT2(D4[3]), .OUT1(D4[2]), .OUT0(D4[1]));  // open: OUT3
  Conditional_Increment_by3 conditional_increment_by3_2 (
    .IN3(conditional_increment_by3_3_out2), .IN2(conditional_increment_by3_3_out1),
    .IN1(conditional_increment_by3_3_out0), .IN0(conditional_increment_by3_11_out3),
    .OUT3(conditional_increment_by3_2_out3), .OUT2(conditional_increment_by3_2_out2),
    .OUT1(conditional_increment_by3_2_out1), .OUT0(conditional_increment_by3_2_out0));
  Conditional_Increment_by3 conditional_increment_by3_3 (
    .IN3(1'b0), .IN2(conditional_increment_by3_4_out3), .IN1(conditional_increment_by3_15_out3),
    .IN0(conditional_increment_by3_13_out3), .OUT3(conditional_increment_by3_3_out3),
    .OUT2(conditional_increment_by3_3_out2), .OUT1(conditional_increment_by3_3_out1),
    .OUT0(conditional_increment_by3_3_out0));
  Conditional_Increment_by3 conditional_increment_by3_4 (
    .IN3(1'b0), .IN2(conditional_increment_by3_23_out3), .IN1(conditional_increment_by3_21_out3),
    .IN0(conditional_increment_by3_19_out3), .OUT3(conditional_increment_by3_4_out3),
    .OUT2(conditional_increment_by3_4_out2), .OUT1(conditional_increment_by3_4_out1),
    .OUT0(conditional_increment_by3_4_out0));
  Conditional_Increment_by3 conditional_increment_by3_5 (
    .IN3(conditional_increment_by3_7_out2), .IN2(conditional_increment_by3_7_out1),
    .IN1(conditional_increment_by3_7_out0), .IN0(conditional_increment_by3_8_out3), .OUT3(D4[0]),
    .OUT2(D3[3]), .OUT1(D3[2]), .OUT0(D3[1]));
  Conditional_Increment_by3 conditional_increment_by3_6 (
    .IN3(conditional_increment_by3_8_out2), .IN2(conditional_increment_by3_8_out1),
    .IN1(conditional_increment_by3_8_out0), .IN0(conditional_increment_by3_30_out3), .OUT3(D3[0]),
    .OUT2(D2[3]), .OUT1(D2[2]), .OUT0(D2[1]));
  Conditional_Increment_by3 conditional_increment_by3_7 (
    .IN3(conditional_increment_by3_2_out2), .IN2(conditional_increment_by3_2_out1),
    .IN1(conditional_increment_by3_2_out0), .IN0(conditional_increment_by3_9_out3),
    .OUT3(conditional_increment_by3_7_out3), .OUT2(conditional_increment_by3_7_out2),
    .OUT1(conditional_increment_by3_7_out1), .OUT0(conditional_increment_by3_7_out0));
  Conditional_Increment_by3 conditional_increment_by3_8 (
    .IN3(conditional_increment_by3_9_out2), .IN2(conditional_increment_by3_9_out1),
    .IN1(conditional_increment_by3_9_out0), .IN0(conditional_increment_by3_10_out3),
    .OUT3(conditional_increment_by3_8_out3), .OUT2(conditional_increment_by3_8_out2),
    .OUT1(conditional_increment_by3_8_out1), .OUT0(conditional_increment_by3_8_out0));
  Conditional_Increment_by3 conditional_increment_by3_9 (
    .IN3(conditional_increment_by3_11_out2), .IN2(conditional_increment_by3_11_out1),
    .IN1(conditional_increment_by3_11_out0), .IN0(conditional_increment_by3_12_out3),
    .OUT3(conditional_increment_by3_9_out3), .OUT2(conditional_increment_by3_9_out2),
    .OUT1(conditional_increment_by3_9_out1), .OUT0(conditional_increment_by3_9_out0));
  Conditional_Increment_by3 conditional_increment_by3_10 (
    .IN3(conditional_increment_by3_12_out2), .IN2(conditional_increment_by3_12_out1),
    .IN1(conditional_increment_by3_12_out0), .IN0(conditional_increment_by3_33_out3),
    .OUT3(conditional_increment_by3_10_out3), .OUT2(conditional_increment_by3_10_out2),
    .OUT1(conditional_increment_by3_10_out1), .OUT0(conditional_increment_by3_10_out0));
  Conditional_Increment_by3 conditional_increment_by3_11 (
    .IN3(conditional_increment_by3_13_out2), .IN2(conditional_increment_by3_13_out1),
    .IN1(conditional_increment_by3_13_out0), .IN0(conditional_increment_by3_14_out3),
    .OUT3(conditional_increment_by3_11_out3), .OUT2(conditional_increment_by3_11_out2),
    .OUT1(conditional_increment_by3_11_out1), .OUT0(conditional_increment_by3_11_out0));
  Conditional_Increment_by3 conditional_increment_by3_12 (
    .IN3(conditional_increment_by3_14_out2), .IN2(conditional_increment_by3_14_out1),
    .IN1(conditional_increment_by3_14_out0), .IN0(conditional_increment_by3_34_out3),
    .OUT3(conditional_increment_by3_12_out3), .OUT2(conditional_increment_by3_12_out2),
    .OUT1(conditional_increment_by3_12_out1), .OUT0(conditional_increment_by3_12_out0));
  Conditional_Increment_by3 conditional_increment_by3_13 (
    .IN3(conditional_increment_by3_15_out2), .IN2(conditional_increment_by3_15_out1),
    .IN1(conditional_increment_by3_15_out0), .IN0(conditional_increment_by3_16_out3),
    .OUT3(conditional_increment_by3_13_out3), .OUT2(conditional_increment_by3_13_out2),
    .OUT1(conditional_increment_by3_13_out1), .OUT0(conditional_increment_by3_13_out0));
  Conditional_Increment_by3 conditional_increment_by3_14 (
    .IN3(conditional_increment_by3_16_out2), .IN2(conditional_increment_by3_16_out1),
    .IN1(conditional_increment_by3_16_out0), .IN0(conditional_increment_by3_35_out3),
    .OUT3(conditional_increment_by3_14_out3), .OUT2(conditional_increment_by3_14_out2),
    .OUT1(conditional_increment_by3_14_out1), .OUT0(conditional_increment_by3_14_out0));
  Conditional_Increment_by3 conditional_increment_by3_15 (
    .IN3(conditional_increment_by3_4_out2), .IN2(conditional_increment_by3_4_out1),
    .IN1(conditional_increment_by3_4_out0), .IN0(conditional_increment_by3_17_out3),
    .OUT3(conditional_increment_by3_15_out3), .OUT2(conditional_increment_by3_15_out2),
    .OUT1(conditional_increment_by3_15_out1), .OUT0(conditional_increment_by3_15_out0));
  Conditional_Increment_by3 conditional_increment_by3_16 (
    .IN3(conditional_increment_by3_17_out2), .IN2(conditional_increment_by3_17_out1),
    .IN1(conditional_increment_by3_17_out0), .IN0(conditional_increment_by3_18_out3),
    .OUT3(conditional_increment_by3_16_out3), .OUT2(conditional_increment_by3_16_out2),
    .OUT1(conditional_increment_by3_16_out1), .OUT0(conditional_increment_by3_16_out0));
  Conditional_Increment_by3 conditional_increment_by3_17 (
    .IN3(conditional_increment_by3_19_out2), .IN2(conditional_increment_by3_19_out1),
    .IN1(conditional_increment_by3_19_out0), .IN0(conditional_increment_by3_20_out3),
    .OUT3(conditional_increment_by3_17_out3), .OUT2(conditional_increment_by3_17_out2),
    .OUT1(conditional_increment_by3_17_out1), .OUT0(conditional_increment_by3_17_out0));
  Conditional_Increment_by3 conditional_increment_by3_18 (
    .IN3(conditional_increment_by3_20_out2), .IN2(conditional_increment_by3_20_out1),
    .IN1(conditional_increment_by3_20_out0), .IN0(Binary_IN[7]), .OUT3(conditional_increment_by3_18_out3),
    .OUT2(conditional_increment_by3_18_out2), .OUT1(conditional_increment_by3_18_out1),
    .OUT0(conditional_increment_by3_18_out0));
  Conditional_Increment_by3 conditional_increment_by3_19 (
    .IN3(conditional_increment_by3_21_out2), .IN2(conditional_increment_by3_21_out1),
    .IN1(conditional_increment_by3_21_out0), .IN0(conditional_increment_by3_22_out3),
    .OUT3(conditional_increment_by3_19_out3), .OUT2(conditional_increment_by3_19_out2),
    .OUT1(conditional_increment_by3_19_out1), .OUT0(conditional_increment_by3_19_out0));
  Conditional_Increment_by3 conditional_increment_by3_20 (
    .IN3(conditional_increment_by3_22_out2), .IN2(conditional_increment_by3_22_out1),
    .IN1(conditional_increment_by3_22_out0), .IN0(Binary_IN[8]), .OUT3(conditional_increment_by3_20_out3),
    .OUT2(conditional_increment_by3_20_out2), .OUT1(conditional_increment_by3_20_out1),
    .OUT0(conditional_increment_by3_20_out0));
  Conditional_Increment_by3 conditional_increment_by3_21 (
    .IN3(conditional_increment_by3_23_out2), .IN2(conditional_increment_by3_23_out1),
    .IN1(conditional_increment_by3_23_out0), .IN0(conditional_increment_by3_24_out3),
    .OUT3(conditional_increment_by3_21_out3), .OUT2(conditional_increment_by3_21_out2),
    .OUT1(conditional_increment_by3_21_out1), .OUT0(conditional_increment_by3_21_out0));
  Conditional_Increment_by3 conditional_increment_by3_22 (
    .IN3(conditional_increment_by3_24_out2), .IN2(conditional_increment_by3_24_out1),
    .IN1(conditional_increment_by3_24_out0), .IN0(Binary_IN[9]), .OUT3(conditional_increment_by3_22_out3),
    .OUT2(conditional_increment_by3_22_out2), .OUT1(conditional_increment_by3_22_out1),
    .OUT0(conditional_increment_by3_22_out0));
  Conditional_Increment_by3 conditional_increment_by3_23 (
    .IN3(1'b0), .IN2(conditional_increment_by3_27_out3), .IN1(conditional_increment_by3_26_out3),
    .IN0(conditional_increment_by3_25_out3), .OUT3(conditional_increment_by3_23_out3),
    .OUT2(conditional_increment_by3_23_out2), .OUT1(conditional_increment_by3_23_out1),
    .OUT0(conditional_increment_by3_23_out0));
  Conditional_Increment_by3 conditional_increment_by3_24 (
    .IN3(conditional_increment_by3_25_out2), .IN2(conditional_increment_by3_25_out1),
    .IN1(conditional_increment_by3_25_out0), .IN0(Binary_IN[10]), .OUT3(conditional_increment_by3_24_out3),
    .OUT2(conditional_increment_by3_24_out2), .OUT1(conditional_increment_by3_24_out1),
    .OUT0(conditional_increment_by3_24_out0));
  Conditional_Increment_by3 conditional_increment_by3_25 (
    .IN3(conditional_increment_by3_26_out2), .IN2(conditional_increment_by3_26_out1),
    .IN1(conditional_increment_by3_26_out0), .IN0(Binary_IN[11]), .OUT3(conditional_increment_by3_25_out3),
    .OUT2(conditional_increment_by3_25_out2), .OUT1(conditional_increment_by3_25_out1),
    .OUT0(conditional_increment_by3_25_out0));
  Conditional_Increment_by3 conditional_increment_by3_26 (
    .IN3(conditional_increment_by3_27_out2), .IN2(conditional_increment_by3_27_out1),
    .IN1(conditional_increment_by3_27_out0), .IN0(Binary_IN[12]), .OUT3(conditional_increment_by3_26_out3),
    .OUT2(conditional_increment_by3_26_out2), .OUT1(conditional_increment_by3_26_out1),
    .OUT0(conditional_increment_by3_26_out0));
  Conditional_Increment_by3 conditional_increment_by3_27 (
    .IN3(1'b0), .IN2(Binary_IN[15]), .IN1(Binary_IN[14]), .IN0(Binary_IN[13]),
    .OUT3(conditional_increment_by3_27_out3), .OUT2(conditional_increment_by3_27_out2),
    .OUT1(conditional_increment_by3_27_out1), .OUT0(conditional_increment_by3_27_out0));
  Conditional_Increment_by3 conditional_increment_by3_28 (
    .IN3(conditional_increment_by3_30_out2), .IN2(conditional_increment_by3_30_out1),
    .IN1(conditional_increment_by3_30_out0), .IN0(conditional_increment_by3_31_out3), .OUT3(D2[0]),
    .OUT2(D1[3]), .OUT1(D1[2]), .OUT0(D1[1]));
  Conditional_Increment_by3 conditional_increment_by3_29 (
    .IN3(conditional_increment_by3_31_out2), .IN2(conditional_increment_by3_31_out1),
    .IN1(conditional_increment_by3_31_out0), .IN0(Binary_IN[1]), .OUT3(D1[0]), .OUT2(D0[3]), .OUT1(D0[2]),
    .OUT0(D0[1]));
  Conditional_Increment_by3 conditional_increment_by3_30 (
    .IN3(conditional_increment_by3_10_out2), .IN2(conditional_increment_by3_10_out1),
    .IN1(conditional_increment_by3_10_out0), .IN0(conditional_increment_by3_32_out3),
    .OUT3(conditional_increment_by3_30_out3), .OUT2(conditional_increment_by3_30_out2),
    .OUT1(conditional_increment_by3_30_out1), .OUT0(conditional_increment_by3_30_out0));
  Conditional_Increment_by3 conditional_increment_by3_31 (
    .IN3(conditional_increment_by3_32_out2), .IN2(conditional_increment_by3_32_out1),
    .IN1(conditional_increment_by3_32_out0), .IN0(Binary_IN[2]), .OUT3(conditional_increment_by3_31_out3),
    .OUT2(conditional_increment_by3_31_out2), .OUT1(conditional_increment_by3_31_out1),
    .OUT0(conditional_increment_by3_31_out0));
  Conditional_Increment_by3 conditional_increment_by3_32 (
    .IN3(conditional_increment_by3_33_out2), .IN2(conditional_increment_by3_33_out1),
    .IN1(conditional_increment_by3_33_out0), .IN0(Binary_IN[3]), .OUT3(conditional_increment_by3_32_out3),
    .OUT2(conditional_increment_by3_32_out2), .OUT1(conditional_increment_by3_32_out1),
    .OUT0(conditional_increment_by3_32_out0));
  Conditional_Increment_by3 conditional_increment_by3_33 (
    .IN3(conditional_increment_by3_34_out2), .IN2(conditional_increment_by3_34_out1),
    .IN1(conditional_increment_by3_34_out0), .IN0(Binary_IN[4]), .OUT3(conditional_increment_by3_33_out3),
    .OUT2(conditional_increment_by3_33_out2), .OUT1(conditional_increment_by3_33_out1),
    .OUT0(conditional_increment_by3_33_out0));
  Conditional_Increment_by3 conditional_increment_by3_34 (
    .IN3(conditional_increment_by3_35_out2), .IN2(conditional_increment_by3_35_out1),
    .IN1(conditional_increment_by3_35_out0), .IN0(Binary_IN[5]), .OUT3(conditional_increment_by3_34_out3),
    .OUT2(conditional_increment_by3_34_out2), .OUT1(conditional_increment_by3_34_out1),
    .OUT0(conditional_increment_by3_34_out0));
  Conditional_Increment_by3 conditional_increment_by3_35 (
    .IN3(conditional_increment_by3_18_out2), .IN2(conditional_increment_by3_18_out1),
    .IN1(conditional_increment_by3_18_out0), .IN0(Binary_IN[6]), .OUT3(conditional_increment_by3_35_out3),
    .OUT2(conditional_increment_by3_35_out2), .OUT1(conditional_increment_by3_35_out1),
    .OUT0(conditional_increment_by3_35_out0));

  assign D0[0] = Binary_IN[0];
endmodule

module Conditional_Increment_by3 (
  input  IN3,
  input  IN2,
  input  IN1,
  input  IN0,
  output OUT3,
  output OUT2,
  output OUT1,
  output OUT0
);

  wire and_1_out, and_2_out, or_1_out;
  wire [3:0] adder_1_out;

  and and_1 (and_1_out, IN1, IN2);
  and and_2 (and_2_out, IN0, IN2);
  Adder #(.width(4)) adder_1 (.a({IN3, IN2, IN1, IN0}), .b(4'b0011), .out(adder_1_out), .cin(1'b0));  // open: cout
  Multiplexer #(.width(4)) multiplexer_1 (
    .in0({IN3, IN2, IN1, IN0}), .in1(adder_1_out), .out({OUT3, OUT2, OUT1, OUT0}), .sel(or_1_out));
  or or_1 (or_1_out, and_1_out, and_2_out, IN3);
endmodule

module PushButton_Detector (
  input  Button,
  output out_2
);

  wire and_1_out, clock_1_out, d_ff_1_q, d_ff_2_q, d_ff_3_q, d_ff_4_q, d_ff_5_q, d_ff_6_q, d_ff_6_qn;

  Clock clock_1 (.out(clock_1_out));
  D_Flip_Flop d_ff_1 (.D(Button), .clk(clock_1_out), .Q(d_ff_1_q));  // open: Qn, preset, reset
  D_Flip_Flop d_ff_2 (.D(d_ff_1_q), .clk(clock_1_out), .Q(d_ff_2_q));  // open: Qn, preset, reset
  D_Flip_Flop d_ff_3 (.D(d_ff_2_q), .clk(clock_1_out), .Q(d_ff_3_q));  // open: Qn, preset, reset
  and and_1 (and_1_out, d_ff_1_q, d_ff_2_q, d_ff_3_q);
  D_Flip_Flop d_ff_4 (.D(and_1_out), .clk(clock_1_out), .Q(d_ff_4_q));  // open: Qn, preset, reset
  D_Flip_Flop d_ff_5 (.D(d_ff_4_q), .clk(clock_1_out), .Q(d_ff_5_q));  // open: Qn, preset, reset
  D_Flip_Flop d_ff_6 (.D(d_ff_5_q), .clk(clock_1_out), .Q(d_ff_6_q), .Qn(d_ff_6_qn));  // open: preset, reset
  and and_2 (out_2, d_ff_5_q, d_ff_6_qn);

  // Notes on the sheet:
  //   debouncer
  //   synchronizer
  //   rising edge detector
endmodule
