// Logisim project SPM_Logism.circ as structural Verilog: 6 circuits, main circuit main
module main (
  input  [7:0] Y,
  input  [7:0] X,
  input  LD,
  input  R,
  input  CLK,
  output [15:0] P,
  output Product,
  output LED0
);

  wire and_1_out, and_2_out, and_3_out, and_4_out, and_5_out, and_6_out, and_7_out, and_8_out, csadd_1_sum,
       csadd_2_sum, csadd_3_sum, csadd_4_sum, csadd_5_sum, csadd_6_sum, current_y_bit_1_current_y, tcmp_1_s;

  TCMP tcmp_1 (.A(and_1_out), .CLK(CLK), .R(R), .S(tcmp_1_s));
  and and_1 (and_1_out, X[7], current_y_bit_1_current_y);
  and and_2 (and_2_out, X[6], current_y_bit_1_current_y);
  and and_3 (and_3_out, X[5], current_y_bit_1_current_y);
  CSADD csadd_1 (.X(and_2_out), .Y(tcmp_1_s), .R(R), .CLK(CLK), .SUM(csadd_1_sum));
  and and_4 (and_4_out, X[4], current_y_bit_1_current_y);
  and and_5 (and_5_out, X[3], current_y_bit_1_current_y);
  CSADD csadd_2 (.X(and_3_out), .Y(csadd_1_sum), .R(R), .CLK(CLK), .SUM(csadd_2_sum));
  CSADD csadd_3 (.X(and_4_out), .Y(csadd_2_sum), .R(R), .CLK(CLK), .SUM(csadd_3_sum));
  and and_6 (and_6_out, X[2], current_y_bit_1_current_y);
  and and_7 (and_7_out, X[1], current_y_bit_1_current_y);
  CSADD csadd_4 (.X(and_5_out), .Y(csadd_3_sum), .R(R), .CLK(CLK), .SUM(csadd_4_sum));
  and and_8 (and_8_out, X[0], current_y_bit_1_current_y);
  CSADD csadd_5 (.X(and_6_out), .Y(csadd_4_sum), .R(R), .CLK(CLK), .SUM(csadd_5_sum));
  CSADD csadd_6 (.X(and_7_out), .Y(csadd_5_sum), .R(R), .CLK(CLK), .SUM(csadd_6_sum));
  CSADD csadd_7 (.X(and_8_out), .Y(csadd_6_sum), .R(R), .CLK(CLK), .SUM(Product));
  Current_Y_bit current_y_bit_1 (.Y(Y), .R(R), .CLK(CLK), .Current_Y(current_y_bit_1_current_y));
  Product_Load product_load_1 (.Current_P(Product), .LD(LD), .R(R), .CLK(CLK), .Product(P), .Done(LED0));
endmodule

module HA (
  input  D0,
  input  D1,
  output Sum,
  output CO
);

  and and_1 (CO, D0, D1);
  xor xor_1 (Sum, D0, D1);
endmodule

module CSADD (
  input  X,
  input  Y,
  input  R,
  input  CLK,
  output SUM
);

  wire and_1_out, d_ff_2_q, ha_1_co, ha_1_sum, xor_1_out, xor_2_out;

  and and_1 (and_1_out, ha_1_sum, X);
  xor xor_1 (xor_1_out, X, ha_1_sum);
  D_Flip_Flop d_ff_1 (.D(xor_1_out), .clk(CLK), .Q(SUM), .reset(R));  // open: Qn, preset
  HA ha_1 (.D0(Y), .D1(d_ff_2_q), .Sum(ha_1_sum), .CO(ha_1_co));
  D_Flip_Flop d_ff_2 (.D(xor_2_out), .clk(CLK), .Q(d_ff_2_q), .reset(R));  // open: Qn, preset
  xor xor_2 (xor_2_out, and_1_out, ha_1_co);
endmodule

module TCMP (
  input  A,
  input  CLK,
  input  R,
  output S
);

  wire d_ff_1_q, or_1_out, xor_1_out;

  xor xor_1 (xor_1_out, A, d_ff_1_q);
  D_Flip_Flop d_ff_1 (.D(or_1_out), .clk(CLK), .Q(d_ff_1_q), .reset(R));  // open: Qn, preset
  or or_1 (or_1_out, A, d_ff_1_q);
  D_Flip_Flop d_ff_2 (.D(xor_1_out), .clk(CLK), .Q(S), .reset(R));  // open: Qn, preset
endmodule

module Current_Y_bit (
  input  [7:0] Y,
  input  R,
  input  CLK,
  output Current_Y
);

  wire [2:0] counter_1_q;

  Multiplexer #(.select(3)) multiplexer_1 (
    .in0(Y[0]), .in1(Y[1]), .in2(Y[2]), .in3(Y[3]), .in4(Y[4]), .in5(Y[5]), .in6(Y[6]), .in7(Y[7]),
    .out(Current_Y), .sel(counter_1_q));
  Counter #(.max('h7), .width(3)) counter_1 (
    .clr(R), .load(1'b0), .up(1'b1), .count(1'b1), .clk(CLK), .Q(counter_1_q));  // open: D, carry
endmodule

module Product_Load (
  input  Current_P,
  input  LD,
  input  R,
  input  CLK,
  output [15:0] Product,
  output Done
);

  wire not_1_out, shift_register_1_p11;
  wire [3:0] counter_1_q;

  not not_1 (not_1_out, Done);
  // Shift_Register #(.length(16)) shift_register_1: pin names not known; wires that end beside it: Done, R, LD, not_1_out, CLK, Current_P, 1'b0, 1'b0, 1'b0, 1'b0, shift_register_1_p11, 1'b0, 1'b0, 1'b0, 1'b0, 1'b0, 1'b0, 1'b0, 1'b0, shift_register_1_p11, Product[15], Product[14], Product[13], Product[12], Product[11], Product[10], Product[9], Product[8], Product[7], Product[6], Product[5], Product[4]
  Counter #(.max('hf), .width(4)) counter_1 (
    .clr(R), .load(1'b0), .up(1'b1), .count(1'b1), .clk(CLK), .Q(counter_1_q));  // open: D, carry
  Comparator #(.width(4)) comparator_1 (.a(4'b1111), .b(counter_1_q), .eq(Done));  // open: gt, lt
endmodule
